// Logisim project hw3.circ as structural Verilog: 7 circuits, main circuit 1-Bit Adder
module _1_Bit_Adder (
  input  a,
  input  b,
  input  carry_in,
  output sum,
  output carry_out
);

  wire and_1_out, and_2_out, xor_1_out;

  xor xor_1 (xor_1_out, a, b);
  xor xor_2 (sum, xor_1_out, carry_in);
  and and_1 (and_1_out, xor_1_out, carry_in);
  and and_2 (and_2_out, a, b);
  or or_1 (carry_out, and_1_out, and_2_out);

  // Notes on the sheet:
  //   Note: Do NOT move any of the pins already in this circuit. Moving the pins may cause the checkers to fail.
endmodule

module _4_Bit_Adder (
  input  [3:0] a,
  input  [3:0] b,
  input  carry_in,
  output [3:0] sum,
  output carry_out
);

  wire n1_bit_adder_1_carry_out, n1_bit_adder_2_carry_out, n1_bit_adder_3_carry_out;

  _1_Bit_Adder u_1_bit_adder_1 (
    .a(a[0]), .b(b[0]), .carry_in(carry_in), .sum(sum[0]), .carry_out(n1_bit_adder_1_carry_out));
  _1_Bit_Adder u_1_bit_adder_2 (
    .a(a[1]), .b(b[1]), .carry_in(n1_bit_adder_1_carry_out), .sum(sum[1]),
    .carry_out(n1_bit_adder_2_carry_out));
  _1_Bit_Adder u_1_bit_adder_3 (
    .a(a[2]), .b(b[2]), .carry_in(n1_bit_adder_2_carry_out), .sum(sum[2]),
    .carry_out(n1_bit_adder_3_carry_out));
  _1_Bit_Adder u_1_bit_adder_4 (
    .a(a[3]), .b(b[3]), .carry_in(n1_bit_adder_3_carry_out), .sum(sum[3]), .carry_out(carry_out));

  // Notes on the sheet:
  //   Note: Do NOT move any of the pins already in this circuit. Moving the pins may cause the checkers to fail.
endmodule

module _4_Bit_ALU (
  input  [3:0] a,
  input  [3:0] b,
  input  [2:0] operation,
  output [3:0] \output 
);

  wire or_2_out;
  wire [0:0] _3;
  wire [3:0] _1, _2, _4, _5, _6, _7, _8, n4_bit_adder_4_sum, not_1_out, not_2_out, xor_1_out;

  _4_Bit_Adder u_4_bit_adder_1 (.a(a), .b(b), .carry_in(1'b0), .sum(_1));  // open: carry_out
  assign _6 = a & b;  // AND_Gate and_1, 4 bits wide
  assign _7 = a | b;  // OR_Gate or_1, 4 bits wide
  assign xor_1_out = a ^ b;  // XOR_Gate xor_1, 4 bits wide
  _4_Bit_Adder u_4_bit_adder_2 (.a(a), .b(not_1_out), .carry_in(1'b1), .sum(_2));  // open: carry_out
  assign not_1_out = ~b;  // NOT_Gate not_1, 4 bits wide
  _4_Bit_Adder u_4_bit_adder_3 (.a(not_2_out), .b(4'b0000), .carry_in(1'b1), .sum(_4));  // open: carry_out
  assign not_2_out = ~a;  // NOT_Gate not_2, 4 bits wide
  assign _8 = ~xor_1_out;  // NOT_Gate not_3, 4 bits wide
  not not_4 (_3[0], or_2_out);
  or or_2 (or_2_out, a[0], a[1]);
  _4_Bit_Adder u_4_bit_adder_4 (.a(a), .b(a), .carry_in(1'b0), .sum(n4_bit_adder_4_sum));  // open: carry_out
  _4_Bit_Adder u_4_bit_adder_5 (.a(n4_bit_adder_4_sum), .b(a), .carry_in(1'b0), .sum(_5));  // open: carry_out
  Multiplexer #(.select(3), .width(4), .disabled(0), .enable("false")) multiplexer_1 (
    .in0(_1), .in1(_2), .in2({3'b000, _3[0]}), .in3(_4), .in4(_5), .in5(_6), .in6(_7), .in7(_8),
    .out(\output ), .sel(operation));

  // Notes on the sheet:
  //   Note: Do NOT move any of the pins already in this circuit. Moving the pins may cause the checkers to fail.
endmodule

module _16_Bit_Adder (
  input  [15:0] a,
  input  [15:0] b,
  input  carry_in,
  output [15:0] sum,
  output carry_out
);

  wire n4_bit_adder_1_carry_out, n4_bit_adder_2_carry_out, n4_bit_adder_3_carry_out;

  _4_Bit_Adder u_4_bit_adder_1 (
    .a(a[3:0]), .b(b[3:0]), .carry_in(carry_in), .sum(sum[3:0]), .carry_out(n4_bit_adder_1_carry_out));
  _4_Bit_Adder u_4_bit_adder_2 (
    .a(a[7:4]), .b(b[7:4]), .carry_in(n4_bit_adder_1_carry_out), .sum(sum[7:4]),
    .carry_out(n4_bit_adder_2_carry_out));
  _4_Bit_Adder u_4_bit_adder_3 (
    .a(a[11:8]), .b(b[11:8]), .carry_in(n4_bit_adder_2_carry_out), .sum(sum[11:8]),
    .carry_out(n4_bit_adder_3_carry_out));
  _4_Bit_Adder u_4_bit_adder_4 (
    .a(a[15:12]), .b(b[15:12]), .carry_in(n4_bit_adder_3_carry_out), .sum(sum[15:12]), .carry_out(carry_out));

  // Notes on the sheet:
  //   Note: Do NOT move any of the pins already in this circuit. Moving the pins may cause the checkers to fail.
endmodule

module _16_Bit_ALU (
  input  [15:0] a,
  input  [15:0] b,
  input  [2:0] operation,
  output [15:0] \output 
);

  wire or_2_out;
  wire [0:0] _3;
  wire [15:0] _1, _2, _4, _5, _6, _7, _8, n16_bit_adder_3_sum, n16_bit_adder_5_sum, n16_bit_adder_7_sum,
       not_1_out, not_2_out, xor_1_out;

  _16_Bit_Adder u_16_bit_adder_1 (.a(a), .b(b), .carry_in(1'b0), .sum(_1));  // open: carry_out
  assign not_1_out = ~a;  // NOT_Gate not_1, 16 bits wide
  _16_Bit_Adder u_16_bit_adder_2 (.a(not_1_out), .b({16{1'b0}}), .carry_in(1'b1), .sum(_4));  // open: carry_out
  assign _6 = a & b;  // AND_Gate and_1, 16 bits wide
  assign _7 = a | b;  // OR_Gate or_1, 16 bits wide
  assign not_2_out = ~b;  // NOT_Gate not_2, 16 bits wide
  assign _8 = ~xor_1_out;  // NOT_Gate not_3, 16 bits wide
  assign xor_1_out = a ^ b;  // XOR_Gate xor_1, 16 bits wide
  _16_Bit_Adder u_16_bit_adder_3 (.a(a), .b(a), .carry_in(1'b0), .sum(n16_bit_adder_3_sum));  // open: carry_out
  _16_Bit_Adder u_16_bit_adder_4 (.a(a), .b(not_2_out), .carry_in(1'b1), .sum(_2));  // open: carry_out
  _16_Bit_Adder u_16_bit_adder_5 (
    .a(n16_bit_adder_3_sum), .b(a), .carry_in(1'b0), .sum(n16_bit_adder_5_sum));  // open: carry_out
  _16_Bit_Adder u_16_bit_adder_6 (
    .a(n16_bit_adder_7_sum), .b(n16_bit_adder_5_sum), .carry_in(1'b0), .sum(_5));  // open: carry_out
  _16_Bit_Adder u_16_bit_adder_7 (
    .a(n16_bit_adder_5_sum), .b(n16_bit_adder_5_sum), .carry_in(1'b0), .sum(n16_bit_adder_7_sum));  // open: carry_out
  or or_2 (or_2_out, a[0], a[1]);
  not not_4 (_3[0], or_2_out);
  Multiplexer #(.select(3), .width(16), .disabled(0), .enable("false")) multiplexer_1 (
    .in0(_1), .in1(_2), .in2({{15{1'b0}}, _3[0]}), .in3(_4), .in4(_5), .in5(_6), .in6(_7), .in7(_8),
    .out(\output ), .sel(operation));

  // Notes on the sheet:
  //   Note: Do NOT move any of the pins already in this circuit. Moving the pins may cause the checkers to fail.
endmodule

module Adder_Checkers (
);

  wire n1_bit_adder_checker_1_p1, n1_bit_adder_checker_1_p2, n1_bit_adder_checker_1_p3,
       n1_bit_adder_checker_1_p4, n1_bit_adder_checker_1_p5, n1_bit_adder_checker_1_p6,
       n1_bit_adder_checker_1_p7, n4_bit_adder_checker_1_p3, n4_bit_adder_checker_1_p4,
       n4_bit_adder_checker_1_p5, n4_bit_adder_checker_1_p6, n16_bit_adder_checker_1_p3,
       n16_bit_adder_checker_1_p4, n16_bit_adder_checker_1_p5, n16_bit_adder_checker_1_p6;
  wire [3:0] n4_bit_adder_checker_1_p1, n4_bit_adder_checker_1_p2, n4_bit_adder_checker_1_p7;
  wire [15:0] n16_bit_adder_checker_1_p1, n16_bit_adder_checker_1_p2, n16_bit_adder_checker_1_p7;

  // _1_Bit_Adder_Checker 1_bit_adder_checker_1: pin names not known; wires that end beside it: n1_bit_adder_checker_1_p1, n1_bit_adder_checker_1_p2, n1_bit_adder_checker_1_p3, n1_bit_adder_checker_1_p4, n1_bit_adder_checker_1_p5, n1_bit_adder_checker_1_p6, n1_bit_adder_checker_1_p7
  Clock Clock (.out(n1_bit_adder_checker_1_p4));
  // _16_Bit_Adder_Checker 16_bit_adder_checker_1: pin names not known; wires that end beside it: n16_bit_adder_checker_1_p1, n16_bit_adder_checker_1_p2, n16_bit_adder_checker_1_p3, n16_bit_adder_checker_1_p4, n16_bit_adder_checker_1_p5, n16_bit_adder_checker_1_p6, n16_bit_adder_checker_1_p7
  _1_Bit_Adder u_1_bit_adder_1 (
    .a(n1_bit_adder_checker_1_p1), .b(n1_bit_adder_checker_1_p2), .carry_in(n1_bit_adder_checker_1_p3),
    .sum(n1_bit_adder_checker_1_p7), .carry_out(n1_bit_adder_checker_1_p6));
  Button Reset (.out(n1_bit_adder_checker_1_p5));
  _16_Bit_Adder u_16_bit_adder_1 (
    .a(n16_bit_adder_checker_1_p1), .b(n16_bit_adder_checker_1_p2), .carry_in(n16_bit_adder_checker_1_p3),
    .sum(n16_bit_adder_checker_1_p7), .carry_out(n16_bit_adder_checker_1_p6));
  Button Reset_2 (.out(n16_bit_adder_checker_1_p5));
  Clock Clock_2 (.out(n16_bit_adder_checker_1_p4));
  // _4_Bit_Adder_Checker 4_bit_adder_checker_1: pin names not known; wires that end beside it: n4_bit_adder_checker_1_p1, n4_bit_adder_checker_1_p2, n4_bit_adder_checker_1_p3, n4_bit_adder_checker_1_p4, n4_bit_adder_checker_1_p5, n4_bit_adder_checker_1_p6, n4_bit_adder_checker_1_p7
  _4_Bit_Adder u_4_bit_adder_1 (
    .a(n4_bit_adder_checker_1_p1), .b(n4_bit_adder_checker_1_p2), .carry_in(n4_bit_adder_checker_1_p3),
    .sum(n4_bit_adder_checker_1_p7), .carry_out(n4_bit_adder_checker_1_p6));
  Clock Clock_3 (.out(n4_bit_adder_checker_1_p4));
  Button Reset_3 (.out(n4_bit_adder_checker_1_p5));

  // Notes on the sheet:
  //   To use each checker:
  //   1. Click the Reset button with the poke tool.
  //   2. To step through test cases individually, click the Clock with the poke tool.
  //   The keyboard shortcut for enabling and disabling ticks is Ctrl+K, which you may use instead.
  //   3. To step through test cases automatically, select "Simulate" from the menu, then click "Enable Ticks" to make the clocks cycle between 0 and 1 automatically.
  //   Note: The 16-Bit Adder Checker does not test all possible input combinations.
  //   It will test random values of a and b and display how many your adder handled correctly.
  //   If you have no errors after roughly 2000 test cases, you can expect that your adder is correct.
endmodule

module ALU_Checkers (
);

  wire n4_bit_alu_checker_1_p4, n4_bit_alu_checker_1_p5, n16_bit_alu_checker_1_p4, n16_bit_alu_checker_1_p5;
  wire [2:0] n4_bit_alu_checker_1_p3, n16_bit_alu_checker_1_p3;
  wire [3:0] n4_bit_alu_checker_1_p1, n4_bit_alu_checker_1_p2, n4_bit_alu_checker_1_p6;
  wire [15:0] n16_bit_alu_checker_1_p1, n16_bit_alu_checker_1_p2, n16_bit_alu_checker_1_p6;

  // _4_Bit_ALU_Checker 4_bit_alu_checker_1: pin names not known; wires that end beside it: n4_bit_alu_checker_1_p1, n4_bit_alu_checker_1_p2, n4_bit_alu_checker_1_p3, n4_bit_alu_checker_1_p4, n4_bit_alu_checker_1_p5, n4_bit_alu_checker_1_p6
  _4_Bit_ALU u_4_bit_alu_1 (
    .a(n4_bit_alu_checker_1_p1), .b(n4_bit_alu_checker_1_p2), .operation(n4_bit_alu_checker_1_p3),
    .\output (n4_bit_alu_checker_1_p6));
  Clock Clock (.out(n4_bit_alu_checker_1_p4));
  Button Reset (.out(n4_bit_alu_checker_1_p5));
  // _16_Bit_ALU_Checker 16_bit_alu_checker_1: pin names not known; wires that end beside it: n16_bit_alu_checker_1_p1, n16_bit_alu_checker_1_p2, n16_bit_alu_checker_1_p3, n16_bit_alu_checker_1_p4, n16_bit_alu_checker_1_p5, n16_bit_alu_checker_1_p6
  _16_Bit_ALU u_16_bit_alu_1 (
    .a(n16_bit_alu_checker_1_p1), .b(n16_bit_alu_checker_1_p2), .operation(n16_bit_alu_checker_1_p3),
    .\output (n16_bit_alu_checker_1_p6));
  Clock Clock_2 (.out(n16_bit_alu_checker_1_p4));
  Button Reset_2 (.out(n16_bit_alu_checker_1_p5));

  // Notes on the sheet:
  //   To use each checker:
  //   1. Click the Reset button with the poke tool.
  //   2. To step through test cases individually, click the Clock with the poke tool.
  //   The keyboard shortcut for enabling and disabling ticks is Ctrl+K, which you may use instead.
  //   3. To step through test cases automatically, select "Simulate" from the menu, then click "Enable Ticks" to make the clocks cycle between 0 and 1 automatically.
  //   Note: The 16-Bit ALU Checker does not test all possible input combinations.
  //   It will test random values of a and b for each operation and display how many your ALU handled correctly.
  //   If you have no errors after roughly 500 test cases per operation, you can expect that your ALU is correct.
endmodule
