// Logisim project lab3.circ as structural Verilog: 4 circuits, main circuit demorgans
module demorgans (
  input  in_1,
  input  in_2,
  output out_3,
  output out_4
);

  wire and_1_out, not_1_out, not_2_out;

  and and_1 (and_1_out, in_1, in_2);
  not not_1 (not_1_out, in_1);
  or or_1 (out_4, not_1_out, not_2_out);
  not not_2 (not_2_out, in_2);
  not not_3 (out_3, and_1_out);

  // Other names for the same wires on the sheet: A = in_1; B = in_2; U = out_3; V = out_4
endmodule

module NAND (
  input  A,
  input  B,
  output Q
);

  wire transistor_4_out;

  Transistor transistor_1 (.in(1'b1), .out(Q), .gate(A));
  Transistor #(.gate("br")) transistor_2 (.in(1'b1), .out(Q), .gate(B));
  Transistor #(.\type ("n")) transistor_3 (.in(transistor_4_out), .out(Q), .gate(A));
  Transistor #(.\type ("n")) transistor_4 (.in(1'b0), .out(transistor_4_out), .gate(B));
endmodule

module NOT (
  input  A,
  output Q
);

  Transistor transistor_1 (.in(1'b1), .out(Q), .gate(A));
  Transistor #(.\type ("n")) transistor_2 (.in(1'b0), .out(Q), .gate(A));
endmodule

module AND (
  input  A,
  input  B,
  output Q
);

  wire nand_1_q;

  NAND nand_1 (.A(A), .B(B), .Q(nand_1_q));
  NOT not_1 (.A(nand_1_q), .Q(Q));

  // Notes on the sheet:
  //   Note: There should be NO transistors or gates here!
  //   Re-read the instructions if you don't know what to do here
endmodule
